# Fritzing sketch smart_door_photon (saved by Fritzing 0.9.3b)
breadboards: 1

parts:
  Part1 = Photon
  photoregistor = PHOTOCELL [package=photocell-kit]
  LED1 = LED - 5mm [color="Red (633nm)" package="5 mm [THT]"]
  R2 = Resistor [tolerance=±5% resistance=220 package="0603 [SMD]"]
  R3 = Resistor [tolerance=±5% resistance=220 package="0603 [SMD]"]
  Buzzer = Piezo Speaker
  RHT1_Temparature_&_Humidity_Sensor = Humidity and Temperature Sensor RHT03  # not connected
  Magnetic_touch_sensor = FUSE [package=fuse_5mm]

nets:
  N1: Part1.A0, photoregistor.P$1, R2.Pin_1
  N2: Part1.GND, R2.Pin_0, R3.Pin_0, Buzzer.pin1, Magnetic_touch_sensor.2
  N3: Part1.D0, LED1.anode
  N4: Part1.D2, Buzzer.pin2
  N5: Part1.D3, Magnetic_touch_sensor.1
  N6: LED1.cathode, R3.Pin_1
